# Fritzing sketch Arduino-IR-Decode (saved by Fritzing 0.7.1b)
breadboards: 1

parts:
  Arduino1 = Arduino
  U2 = mystery part, 3 pins [chip_label="IR Reciever" spacing=300mil]

nets:
  N1: Arduino1.D2, U2.pin3
  N2: Arduino1.+5V, U2.pin2
  N3: Arduino1.GND, U2.pin1
